# Fritzing sketch snailed-it (saved by Fritzing 1.0.1rc)
stripboards: 1

parts:
  Mod1 = Raspberry Pi 4B
  S5 = Momentary Switch [package=ksa_sealed_tac_switch]
  S6 = Momentary Switch [package=ksa_sealed_tac_switch]
  S7 = Momentary Switch [package=ksa_sealed_tac_switch]
  S8 = Momentary Switch [package=ksa_sealed_tac_switch]
  U2 = RFID RC522 SIP - 8 pins [chip_label="RFID RC522" package="SIP (Single Inline) [THT]"]

nets:
  3V3: Mod1.3V3, U2.VCC
  N1: Mod1.GPIO2, U2.NSS
  GND: Mod1.GND, S5.2, S6.1, S6.2, S7.1, S7.2, S8.1, S8.2, U2.GND
  N2: Mod1.GPIO10, U2.MOSI
  N3: Mod1.GPIO9, U2.MISO
  N4: Mod1.GPIO25, U2.RST
  N5: Mod1.GPIO11, U2.SCK
  N6: Mod1.GPIO6, S8.3, S8.4
  N7: Mod1.GPIO13, S7.3, S7.4
  N8: Mod1.GPIO19, S6.3, S6.4
  N9: Mod1.GPIO26, S5.4

custom parts:
  RFID RC522 SIP - 8 pins: A SIP stand-in part for RFID RC522 . With 8 pins on a 300 mil single inline package (SIP) footprint.
